# Fritzing sketch Midterm Embedded (saved by Fritzing 0.9.3b)

parts:
  Part1 = Solid State High Level Relay Module [package=relay]
  Part2 = Solid State High Level Relay Module [package=relay]
  Mod1 = Raspberry Pi 4B
  IC1 = Rasberry Pi NIOR Camera [chip_label=IC package="DIP (Dual Inline) [THT]"]  # not connected
  Part3 = Adafruit MLX90640 Thermal Camera [part_number="Adafruit #4407"]
  S1 = Toggle Switch [package=THT]
  PIR1 = PIR sensor

nets:
  N1: Part1.CH1, Mod1.GPIO24
  N2: Part2.DC+, Mod1.5V
  N3: Part2.CH1, Mod1.GPIO23
  GND: Part2.DC-, Mod1.GND, S1.COM, PIR1.GND
  3V3: Mod1.3V3, PIR1.VDD
  N4: Mod1.GPIO2, Part3.SDA
  N5: Mod1.GPIO3, Part3.SCL
  N6: Mod1.GPIO22, PIR1.SIG
  N7: Mod1.GPIO16, S1.L1
  N8: Mod1.GPIO20, S1.L2

notes:
  240 VAC
  Open Door Actuator
  Close Door Actuator
  MLX90614 Temperature Sensor
  Raspberry Pi 4 4GB
  Raspberry Pi 4 Camera V2 8MP
  Connect to 7 inch display
  Slide Switch
  Gray - Mask and Body Temp. Check Mode
  Orange - Surveillance Social Distancing Cam. Mode
  PIR Sensor

custom parts:
  Solid State High Level Relay Module: 5V Omron solid state relay 240V 2A output with resistance fuse.
  Rasberry Pi NIOR Camera: Camera
  Adafruit MLX90640 Thermal Camera: You can now add affordable heat-vision to your project and with an Adafruit MLX90640 Thermal Camera Breakout. This sensor contains a 24x32 array of IR thermal sensors. When connected to your microcontroller (or Raspberry Pi) it will return an array of 768 individual infrared temperature readings over I2C. It's like those fancy thermal cameras, but compact and simple enough for easy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
